# Fritzing sketch Drive controller (saved by Fritzing 0.9.3b)

parts:
  A1 = Arduino Nano (Rev3.0)
  M1 = DC Motor
  M2 = DC Motor
  U1-1 = HALL-EFFECT [package=sc70]
  U1-2 = HALL-EFFECT [package=sc70]
  V2 = DC Power [voltage=12V]
  U2-1 = HALL-EFFECT [package=sc70]
  U2-2 = HALL-EFFECT [package=sc70]
  U1 = SPDT Slide Switch [package=ayz0202]
  LED1 = LEDs [package=led10mm]
  LED2 = LEDs [package=led10mm]
  LED3 = LEDs [package=led10mm]
  LED4 = LEDs [package=led10mm]
  R1 = Resistor [tolerance=±5% resistance=680 package=THT]
  R2 = Resistor [tolerance=±5% resistance=680 package=THT]
  R3 = Resistor [tolerance=±5% resistance=680 package=THT]
  R4 = Resistor [tolerance=±5% resistance=680 package=THT]
  U2 = VNH2SP30 [package=vnh2sp30]
  U3 = VNH2SP30 [package=vnh2sp30]
  R5 = Resistor [tolerance=±5% resistance=10k package=THT]
  R6 = Resistor [tolerance=±5% resistance=10k package=THT]

nets:
  GND: A1.GND, U1-1.GND, U1-2.GND, V2.V-, U2-1.GND, U2-2.GND, R1.Pin_0, R2.Pin_0, R3.Pin_0, R4.Pin_0, U2.GNDB, U2.GNDA, U3.GNDB, U3.GNDA
  N1: A1.D2, U3.INA
  N2: A1.D3, U3.PWM
  N3: A1.D4, U3.INB
  N4: A1.D5, U2.PWM
  N5: A1.D6, LED1.A
  N6: A1.D7, U2.INA
  N7: A1.D8, U2.INB
  N8: A1.D9, LED2.A
  N9: A1.D10, LED3.A
  N10: A1.D11/MOSI, LED4.A
  VCC: A1.VIN, U1.2, U1.5, U2.VCC, U3.VCC
  VCC_2: A1.5V, U1-1.VCC, U1-2.VCC, U2-1.VCC, U2-2.VCC, R6.Pin_1
  N11: A1.A7, U2.EN_DIAA, R5.Pin_0
  N12: A1.A6, U3.EN_DIAA, R6.Pin_0
  N13: A1.A5, U2.CS
  N14: A1.A4, U3.CS
  N15: A1.A3, U2-1.OUT
  N16: A1.A2, U2-2.OUT
  N17: A1.A1, U1-2.OUT
  N18: A1.A0, U1-1.OUT
  N19: M1.pin_1, U3.OUTA
  N20: M1.pin_2, U3.OUTB
  N21: M2.pin_1, U2.OUTB
  N22: M2.pin_2, U2.OUTA
  N23: V2.V+, U1.3, U1.6
  N24: LED1.C, R4.Pin_1
  N25: LED2.C, R3.Pin_1
  N26: LED3.C, R2.Pin_1
  N27: LED4.C, R1.Pin_1
